# Fritzing sketch hello_lightbulb (saved by Fritzing 0.7.11b)
breadboards: 1

parts:
  Arduino_Ethernet_Shield1 = Arduino Ethernet Shield
  R1 = Resistor [tolerance=±5% resistance=100 package=THT]
  R2 = Resistor [tolerance=±5% resistance=10k package=THT]
  BUTTON1 = Arcade Button (yellow)
  LED1 = LED - 5mm [color="Red (633nm)" package="5 mm [THT]"]
  R3 = Resistor [tolerance=±5% resistance=1k package=THT]

nets:
  N1: Arduino_Ethernet_Shield1.D7, R1.Pin_0
  N2: Arduino_Ethernet_Shield1.D6, R3.Pin_0
  N3: Arduino_Ethernet_Shield1.+5V, BUTTON1.no_name_yet#2
  N4: Arduino_Ethernet_Shield1.GND, R2.Pin_0, LED1.cathode
  N5: R1.Pin_1, R2.Pin_1, BUTTON1.no_name_yet#1
  N6: LED1.anode, R3.Pin_1

custom parts:
  Arcade Button (yellow): Adafruit Arcade Button (yellow)
