# Fritzing sketch NO2Sensor (saved by Fritzing 0.8.3b)
breadboards: 1

parts:
  Part1 = Arduino Uno (Rev3)
  R1 = Resistor [tolerance=±5% resistance=2.2k package=THT]
  R2 = Resistor [tolerance=±5% resistance=100 package=THT]
  R3 = Resistor [tolerance=±5% resistance=27 package=THT]
  S1 = Pushbutton [package="[THT]"]

nets:
  N1: Part1.A3, Part1.GND, R1.Pin_0, R2.Pin_0, S1.Pin_1, S1.Pin_2, S1.Pin_3, S1.Pin_4
  N2: Part1.5V, R1.Pin_1, R3.Pin_1
  N3: R2.Pin_1, R3.Pin_0
