# Fritzing sketch pressure_mat (saved by Fritzing 0.8.3b)
breadboards: 1

parts:
  R1 = Resistor [tolerance=±5% resistance=100 package=THT]
  R2 = Resistor [tolerance=±5% resistance=10k package=THT]
  LED1 = LED - 5mm [color="Red (633nm)" package="5 mm [THT]"]
  R3 = Resistor [tolerance=±5% resistance=1k package=THT]
  Part1 = Arduino Board Ethernet
  R4 = Textile Pushbutton [part_number="TACRACPS1X0404GY "]

nets:
  N1: R1.Pin_0, Part1.D7
  N2: R1.Pin_1, R2.Pin_1, R4.leg0
  N3: R2.Pin_0, LED1.cathode, Part1.GND
  N4: LED1.anode, R3.Pin_1
  N5: R3.Pin_0, Part1.D6_PWM
  N6: Part1.5V, R4.leg1
