# Fritzing sketch WindSensor (saved by Fritzing 0.8.3b)
breadboards: 1

parts:
  Part1 = Arduino Board Ethernet
  LED1 = LED - 5mm [color="Yellow (592nm)" package="5 mm [THT]"]
  R1 = Resistor [tolerance=±5% resistance=220 package=THT]
  U1 = mystery part, 3 pins [chip_label=?]

nets:
  N1: Part1.D9_PWM, LED1.cathode
  N2: Part1.A0, U1.pin3
  N3: Part1.5V, U1.pin2
  N4: Part1.GND, R1.Pin_0, U1.pin1
  N5: LED1.anode, R1.Pin_1
