# Fritzing sketch WeatherStation (saved by Fritzing 0.8.3b)
circuit board: 6.9215cm x 5.33756cm
breadboards: 1

parts:
  10kΩ = Resistor [tolerance=±5% resistance=10k package=THT]
  DHT-22 = Humidity and Temperature Sensor RHT03
  Part2 = Arduino Mega 2560 (Rev3)
  Part3 = Arduino Ethernet Shield (Rev3)

nets:
  5V: 10kΩ.Pin_0, DHT-22.Vcc, Part2.5V, Part3.5V
  N1: 10kΩ.Pin_1, DHT-22.Data-signal, Part2.D2_PWM, Part3.D2
  GND: DHT-22.GND_2, Part2.GND, Part3.GND
  N2: Part2.A0, Part3.A0
  N3: Part2.A1, Part3.A1
  N4: Part2.A2, Part3.A2
  N5: Part2.A3, Part3.A3
  N6: Part2.A4, Part3.A4/SDA
  N7: Part2.A5, Part3.A5/SCL
  N8: Part2.D13_PWM, Part3.SPI/D13
  N9: Part2.D12_PWM, Part3.SPI/D12
  N10: Part2.D11_PWM, Part3.PWM_D11
  N11: Part2.D10_PWM, Part3.ETH_CS
  N12: Part2.D9_PWM, Part3.PWM_D9
  N13: Part2.D8_PWM, Part3.D8
  N14: Part2.IOREF#254, Part3.N/A
  N15: Part2.IOREF#255, Part3.IOREF
  N16: Part2.RESET, Part3.RESET
  3V3: Part2.3V3, Part3.3V3
  VIN: Part2.VIN, Part3.VIN
  N17: Part2.D0_RX0, Part3.RX/D0
  N18: Part2.D1_TX0, Part3.TX/D1
  N19: Part2.D3_PWM, Part3.PWM_D3
  N20: Part2.D4_PWM, Part3.SDCS
  N21: Part2.D5_PWM, Part3.PWM_D5
  N22: Part2.D6_PWM, Part3.PWM_D6
  N23: Part2.D7_PWM, Part3.D7

notes:
  Data Sensing Lab
  Babilim Light Industries
  Data Sensing Lab, DHT-22 Sensor, 0.5
