# Fritzing sketch WeatherStationXBeeWiFi (saved by Fritzing 0.8.3b)
circuit board: 6.9215cm x 5.33756cm
breadboards: 1

parts:
  10kΩ = Resistor [tolerance=±5% resistance=10k package=THT]
  DHT-22 = Humidity and Temperature Sensor RHT03
  Part2 = Arduino Leonardo (Rev3b)
  Part3 = Arduino Wireless SD Shield

nets:
  VCC: 10kΩ.Pin_0, DHT-22.Vcc, Part2.5V, Part3.+5V
  N1: 10kΩ.Pin_1, DHT-22.Data-signal, Part2.D2/SDA, Part3.D2
  GND: DHT-22.GND_2, Part2.GND, Part3.GND
  N2: Part2.D0/RX, Part3.ARDUINO-RX(0)
  N3: Part2.D1/TX, Part3.ARDUINO-TX(1)
  N4: Part2.D3_PWM/SCL, Part2.SCL, Part3.D3
  N5: Part2.D4/A6, Part3.SD_CS
  N6: Part2.D5_PWM, Part3.D5
  N7: Part2.D6_PWM/A7, Part3.D6
  N8: Part2.D7, Part3.D7
  N9: Part2.RESET, Part3.RESET
  3V3: Part2.3V3, Part3.3.3V
  VIN: Part2.VIN, Part3.VIN
  N10: Part2.A0, Part3.A0
  N11: Part2.A1, Part3.A1
  N12: Part2.A2, Part3.A2
  N13: Part2.A3, Part3.A3
  N14: Part2.A4, Part3.A4
  N15: Part2.A5, Part3.A5
  N16: Part2.D8/A8, Part3.D8
  N17: Part2.D9_PWM/A9, Part3.D9
  N18: Part2.D10_PWM/A10, Part3.D10
  N19: Part2.D11_PWM, Part3.D11
  N20: Part2.D12/A11, Part3.D12
  N21: Part2.D13_PWM, Part3.D13
  N22: Part2.AREF, Part3.AREF

notes:
  Data Sensing Lab
  Babilim Light Industries
  Data Sensing Lab, DHT-22 Sensor, 0.5
